# Fritzing sketch neopixel_wall_clock (saved by Fritzing 0.9.2b)
breadboards: 1

parts:
  Part1 = Arduino Nano (Rev3.0)
  neopixel1 = Neopixel Ring 12
  NEOPIXEL2 = Neopixel Strip -- Black (30/m)
  S1 = Pushbutton [package="[SMD]"]
  R1 = PHOTOCELL [package=photocell]
  BATT1 = 4xAA Switchable Battery Pack w/Bare Wire
  S2 = Toggle Switch [package=THT]
  R2 = Resistor [tolerance=±5% resistance=10k package=THT]
  R3 = Resistor [tolerance=±5% resistance=10k package=THT]
  U1 = POT [package=pot_mammoth]

nets:
  GND: Part1.GND, neopixel1.GND, NEOPIXEL2.GND, BATT1.NEG, R2.Pin_0, R3.Pin_1, U1.S
  N1: Part1.D3, neopixel1.IN
  N2: Part1.D12/MISO, S1.Pin_1, S1.Pin_2, R2.Pin_1
  VIN: Part1.VIN, neopixel1.VCC, NEOPIXEL2.+5V, S1.Pin_3, S1.Pin_4, R1.P$1, S2.COM, U1.E
  N3: Part1.A3, U1.A
  N4: Part1.A0, R1.P$2, R3.Pin_0
  N5: neopixel1.OUT, NEOPIXEL2.Din
  N6: BATT1.POS, S2.L2

custom parts:
  Neopixel Ring 12: Neopixel Ring x12
  Neopixel Strip -- Black (30/m): These NeoPixel strips have 30 digitally-addressable pixel LEDs per meter and are very affordable and are only 12.5 mm wide, 10 mm if you remove the strip from the casing.
  4xAA Switchable Battery Pack w/Bare Wire: 4xAA Switchable Battery Pack with Bare Wire connection
